// Logisim project s-mips.circ as structural Verilog
module S_MIPS_Board (
  input  DESHABILITAR_DISPATCHER,
  output halt
);

  wire button_1_out, CLK, CS, d_ff_1_q, LCLR, LoadRAM, LoadRAMOn, LW, R_R_W, R_W, ram_dispatcher_1_finished,
       RCS, Reset_out, RST, TTY_EN;
  wire [2:0] KDB;
  wire [3:0] LMask, Mask, ram_1_read_time, ram_1_write_time, RMask;
  wire [6:0] KDB_DATA, TTY_DATA;
  wire [15:0] Addr, LAddr, RAddr;
  wire [31:0] I0, I1, I2, I3, LData, ram_1_data_out_0, ram_1_data_out_1, ram_1_data_out_2, ram_1_data_out_3,
       RI0, RI1, RI2, RI3;

  TTY #(.rows(25), .cols(80)) tty_1 (.data(TTY_DATA), .clk(CLK), .we(TTY_EN), .clr(RST));
  not not_1 (LoadRAMOn, ram_dispatcher_1_finished);
  RAM_Dispatcher ram_dispatcher_1 (
    .WriteTime(ram_1_write_time), .Clock(CLK), .Data(LData), .Address(LAddr), .Mask(LMask),
    .Finished(ram_dispatcher_1_finished), .Write(LW), .CLR(LCLR));
  Keyboard #(.buflen(64)) keyboard_1 (.clk(CLK), .re(KDB[0]), .avail(KDB[2]), .data(KDB_DATA));  // open: clr
  RAM ram_1 (
    .Address(RAddr), .Data_Out_0(ram_1_data_out_0), .Data_Out_1(ram_1_data_out_1),
    .Data_Out_2(ram_1_data_out_2), .Data_Out_3(ram_1_data_out_3), .Data_In_0(RI0), .Data_In_1(RI1),
    .Data_In_2(RI2), .Data_In_3(RI3), .Mask(RMask), .nRead_Write(R_R_W), .Chip_Select(RCS),
    .Read_Time(ram_1_read_time), .Reset(button_1_out), .Write_Time(ram_1_write_time));
  Button button_1 (.out(button_1_out));
  D_Flip_Flop d_ff_1 (.clk(CLK), .D(1'b1), .Q(d_ff_1_q), .reset(Reset_out));  // open: Qn, preset, en
  Button Reset (.out(Reset_out));
  S_MIPS s_mips_1 (
    .Kbd_Enable(KDB[0]), .Address(Addr), .Kbd_Clear(KDB[1]), .Kbd_Available(KDB[2]), .RAM_In_0(I0),
    .Kbd_ASCII_Data(KDB_DATA), .RAM_In_1(I1), .TTY_Enable(TTY_EN), .RAM_In_2(I2), .RAM_In_3(I3),
    .TTY_ASCII_Data(TTY_DATA), .Reset(RST), .RAM_Out_0(ram_1_data_out_0), .Clock(CLK),
    .RAM_Out_1(ram_1_data_out_1), .Stop(halt), .RAM_Out_2(ram_1_data_out_2), .RAM_Out_3(ram_1_data_out_3),
    .Mask(Mask), .Read_Time(ram_1_read_time), .Write_Time(ram_1_write_time), .nRead_Write(R_W),
    .Chip_Select(CS));
  D_Flip_Flop d_ff_2 (.clk(CLK), .D(d_ff_1_q), .Qn(LCLR), .reset(Reset_out));  // open: Q, preset, en
  or or_1 (RST, LCLR, LoadRAM);
  Clock clock_1 (.out(CLK));
  Multiplexer #(.width(32), .enable("false")) multiplexer_1 (.in0(I0), .in1(LData), .out(RI0), .sel(LoadRAM));
  Multiplexer #(.width(32), .enable("false")) multiplexer_2 (.in0(I1), .in1(LData), .out(RI1), .sel(LoadRAM));
  Multiplexer #(.width(32), .enable("false")) multiplexer_3 (.in0(I2), .in1(LData), .out(RI2), .sel(LoadRAM));
  Multiplexer #(.width(32), .enable("false")) multiplexer_4 (.in0(I3), .in1(LData), .out(RI3), .sel(LoadRAM));
  and and_1 (LoadRAM, ~DESHABILITAR_DISPATCHER, LoadRAMOn);  // AND_Gate
  Multiplexer #(.width(16), .enable("false")) multiplexer_5 (.in0(Addr), .in1(LAddr), .out(RAddr), .sel(LoadRAM));
  Multiplexer #(.width(4), .enable("false")) multiplexer_6 (.in0(Mask), .in1(LMask), .out(RMask), .sel(LoadRAM));
  Multiplexer #(.enable("false")) multiplexer_7 (.in0(CS), .in1(LW), .out(RCS), .sel(LoadRAM));
  Multiplexer #(.enable("false")) multiplexer_8 (.in0(R_W), .in1(LW), .out(R_R_W), .sel(LoadRAM));

  // Notes on the sheet:
  //   NO MODIFICAR
  //   Keyboard
endmodule

module RAM (
  input  [15:0] Address,
  input  [31:0] Data_In_0,
  input  [31:0] Data_In_1,
  input  [31:0] Data_In_2,
  input  [31:0] Data_In_3,
  input  [3:0] Mask,
  input  nRead_Write,
  input  Chip_Select,
  input  Reset,
  output [31:0] Data_Out_0,
  output [31:0] Data_Out_1,
  output [31:0] Data_Out_2,
  output [31:0] Data_Out_3,
  output [3:0] Read_Time,
  output [3:0] Write_Time
);

  wire and_2_out, and_3_out, and_4_out, and_5_out, and_6_out, and_7_out, and_8_out, and_9_out, Changed, CLK,
       comparator_2_eq, comparator_3_eq, comparator_4_eq, comparator_5_eq, comparator_6_eq, Count,
       demultiplexer_3_out0, Idle, Idle_q, Load, Load0, Load1, nand_1_out, or_1_out, or_2_out, or_3_out,
       or_4_out, or_5_out, or_6_out, or_7_out, or_8_out, or_9_out, or_10_out, Proc_q, Update_Mem, Zero_Time;
  wire [3:0] counter_1_q, multiplexer_1_out, subtractor_1_out;
  wire [31:0] register_1_q, register_2_q, register_3_q, register_4_q, register_5_q;

  // Probe on 4'b0011
  // Probe on 4'b0010
  Multiplexer #(.width(4), .enable("false")) multiplexer_1 (
    .in0(4'b0011), .in1(4'b0010), .out(multiplexer_1_out), .sel(nRead_Write));
  or or_1 (or_1_out, Idle, Update_Mem);
  or or_2 (or_2_out, ~Chip_Select, Reset);  // OR_Gate
  Subtractor #(.width(4)) subtractor_1 (.a(multiplexer_1_out), .b(4'b0010), .out(subtractor_1_out));  // open: bin, bout
  D_Flip_Flop u_Idle (.clk(CLK), .D(or_1_out), .Q(Idle_q), .preset(or_2_out));  // open: Qn, en, reset
  Demultiplexer #(.enable("false")) demultiplexer_1 (.out0(Idle), .out1(Load0), .in(Idle_q), .sel(Changed));
  // Probe on counter_1_q
  Counter #(.width(4), .max('hf)) counter_1 (
    .load(Load), .D(subtractor_1_out), .count(Count), .Q(counter_1_q), .clk(CLK), .clr(or_3_out));  // open: carry
  or or_3 (or_3_out, ~Chip_Select, Reset);  // OR_Gate
  Comparator #(.width(4), .mode("unsigned")) comparator_1 (
    .a(4'b0000), .b(counter_1_q), .eq(Zero_Time));  // open: gt, lt
  or or_4 (or_4_out, Count, Load0, Load1);
  Register #(.width(32)) register_1 (.D(Data_In_0), .en(Chip_Select), .Q(register_1_q), .clk(CLK), .clr(or_5_out));
  or or_5 (or_5_out, ~Chip_Select, Reset);  // OR_Gate
  Register #(.width(32)) register_2 (.D(Data_In_1), .en(Chip_Select), .Q(register_2_q), .clk(CLK), .clr(or_6_out));
  or or_6 (or_6_out, ~Chip_Select, Reset);  // OR_Gate
  Register #(.width(32)) register_3 (.D(Data_In_2), .en(Chip_Select), .Q(register_3_q), .clk(CLK), .clr(or_7_out));
  or or_7 (or_7_out, ~Chip_Select, Reset);  // OR_Gate
  Register #(.width(32)) register_4 (.D(Data_In_3), .en(Chip_Select), .Q(register_4_q), .clk(CLK), .clr(or_8_out));
  or or_8 (or_8_out, ~Chip_Select, Reset);  // OR_Gate
  Register #(.width(32)) register_5 (
    .D({{11{1'b1}}, nRead_Write, Mask, Address}), .en(Chip_Select), .Q(register_5_q), .clk(CLK),
    .clr(or_9_out));
  or or_9 (or_9_out, ~Chip_Select, Reset);  // OR_Gate
  D_Flip_Flop Proc (.clk(CLK), .D(or_4_out), .Q(Proc_q), .reset(or_10_out));  // open: Qn, preset, en
  or or_10 (or_10_out, ~Chip_Select, Reset);  // OR_Gate
  Demultiplexer #(.enable("false")) demultiplexer_2 (
    .out0(Count), .out1(Update_Mem), .in(demultiplexer_3_out0), .sel(Zero_Time));
  Demultiplexer #(.enable("false")) demultiplexer_3 (
    .out0(demultiplexer_3_out0), .out1(Load1), .in(Proc_q), .sel(Changed));
  Clock clock_1 (.out(CLK));
  Comparator #(.width(32)) comparator_2 (.a(register_1_q), .b(Data_In_0), .eq(comparator_2_eq));  // open: gt, lt
  Comparator #(.width(32)) comparator_3 (.a(register_2_q), .b(Data_In_1), .eq(comparator_3_eq));  // open: gt, lt
  Comparator #(.width(32)) comparator_4 (.a(register_3_q), .b(Data_In_2), .eq(comparator_4_eq));  // open: gt, lt
  Comparator #(.width(32)) comparator_5 (.a(register_4_q), .b(Data_In_3), .eq(comparator_5_eq));  // open: gt, lt
  Comparator #(.width(32)) comparator_6 (
    .a(register_5_q), .b({{11{1'b1}}, nRead_Write, Mask, Address}), .eq(comparator_6_eq));  // open: gt, lt
  nand nand_1 (nand_1_out, comparator_6_eq, comparator_2_eq, comparator_3_eq, comparator_4_eq, comparator_5_eq);
  and and_1 (Changed, nand_1_out, Chip_Select);
  or or_11 (Load, Count, Load1, Load0);
  and and_2 (and_2_out, Mask[0], Update_Mem, nRead_Write);
  and and_3 (and_3_out, Mask[1], Update_Mem, nRead_Write);
  and and_4 (and_4_out, Mask[2], Update_Mem, nRead_Write);
  and and_5 (and_5_out, Mask[3], Update_Mem, nRead_Write);
  RAM_part #(.addrWidth(16), .dataWidth(32), .bus("separate")) ram_1 (
    .addr(Address), .din(Data_In_0), .data(Data_Out_0), .str(and_2_out), .sel(Chip_Select), .clk(CLK),
    .ld(and_6_out), .clr(Reset));
  and and_6 (and_6_out, ~nRead_Write, Idle);  // AND_Gate
  RAM_part #(.addrWidth(16), .dataWidth(32), .bus("separate")) ram_2 (
    .addr(Address), .din(Data_In_1), .data(Data_Out_1), .str(and_3_out), .sel(Chip_Select), .clk(CLK),
    .ld(and_7_out), .clr(Reset));
  and and_7 (and_7_out, ~nRead_Write, Idle);  // AND_Gate
  RAM_part #(.addrWidth(16), .dataWidth(32), .bus("separate")) ram_3 (
    .addr(Address), .din(Data_In_2), .data(Data_Out_2), .str(and_4_out), .sel(Chip_Select), .clk(CLK),
    .ld(and_8_out), .clr(Reset));
  and and_8 (and_8_out, ~nRead_Write, Idle);  // AND_Gate
  RAM_part #(.addrWidth(16), .dataWidth(32), .bus("separate")) ram_4 (
    .addr(Address), .din(Data_In_3), .data(Data_Out_3), .str(and_5_out), .sel(Chip_Select), .clk(CLK),
    .ld(and_9_out), .clr(Reset));
  and and_9 (and_9_out, ~nRead_Write, Idle);  // AND_Gate

  assign Read_Time = 4'b0011;
  assign Write_Time = 4'b0010;

  // Other names for the same wires on the sheet: M0 = Mask[0]; M1 = Mask[1]; M2 = Mask[2]; M3 = Mask[3];
  //   RW = nRead_Write; CLR = Reset; CS = Chip_Select; Load2 = Count

  // Notes on the sheet:
  //   NO MODIFICAR
  //   excepto quizás los valores RT y WT
  //   BANK0
  //   BANK1
  //   BANK2
  //   BANK3
endmodule

module S_MIPS (
  input  Kbd_Available,
  input  [6:0] Kbd_ASCII_Data,
  input  [31:0] RAM_Out_0,
  input  [31:0] RAM_Out_1,
  input  Reset,
  input  [31:0] RAM_Out_2,
  input  Clock,
  input  [31:0] RAM_Out_3,
  input  [3:0] Read_Time,
  input  [3:0] Write_Time,
  output Kbd_Enable,
  output [15:0] Address,
  output Kbd_Clear,
  output TTY_Enable,
  output [6:0] TTY_ASCII_Data,
  output Stop,
  output [31:0] RAM_In_0,
  output [31:0] RAM_In_1,
  output [31:0] RAM_In_2,
  output [31:0] RAM_In_3,
  output [3:0] Mask,
  output nRead_Write,
  output Chip_Select
);

  wire control_unit_1_alua, control_unit_1_dout_sel, control_unit_1_out_7, control_unit_1_unsigned,
       control_unit_1_writepc, control_unit_1_writerf, CS_In, DIn_SEL, END_CS, flag, RAM_RW_In;
  wire [1:0] control_unit_1_alub, control_unit_1_bcselector, control_unit_1_rf_sel, MA_SEL, offset;
  wire [2:0] control_unit_1_flagselector, control_unit_1_rfinput;
  wire [3:0] control_unit_1_alu_sel;
  wire [5:0] func_code, op_code;
  wire [31:0] DataPath_Out, little_endian_1_output, multiplexer_1_out, multiplexer_2_out, multiplexer_3_out,
       RAM_Output;

  Data_Path_2 data_path_1 (
    .CLK(Clock), .Reset(Reset), .RegDest(control_unit_1_rf_sel), .MemtoReg(control_unit_1_rfinput),
    .ALUSrcA(control_unit_1_alua), .ALUSrcB(control_unit_1_alub), .ALUControl(control_unit_1_alu_sel),
    .in_8(control_unit_1_flagselector), .in_9(control_unit_1_dout_sel), .in_10(control_unit_1_writepc),
    .in_11(MA_SEL), .DataIn(multiplexer_2_out), .op_code(op_code), .func(func_code), .Flag(flag),
    .Data_Out(DataPath_Out), .Mask(Mask), .TTY_DATA(TTY_ASCII_Data), .Offset(offset), .Address(Address),
    .in_12(control_unit_1_bcselector), .in_13(control_unit_1_writerf), .in_14(control_unit_1_out_7),
    .in_15(control_unit_1_unsigned));
  Multiplexer #(.width(32), .enable("false")) multiplexer_1 (
    .in0({32{1'b1}}), .in1({{18{1'b0}}, Kbd_ASCII_Data[6], {7{1'b0}}, Kbd_ASCII_Data[5:0]}),
    .out(multiplexer_1_out), .sel(Kbd_Available));
  Multiplexer #(.width(32), .enable("false")) multiplexer_2 (
    .in0(RAM_Output), .in1(multiplexer_1_out), .out(multiplexer_2_out), .sel(DIn_SEL));
  RAMRW ramrw_1 (
    .Read_Time(Read_Time), .Write_Time(Write_Time), .in_3(Clock), .in_4(Reset), .CS_In(CS_In),
    .RWSrc(RAM_RW_In), .END(END_CS), .CS(Chip_Select), .RW(nRead_Write));
  Little_Endian little_endian_1 (.Input(DataPath_Out), .Output(little_endian_1_output));
  Multiplexer #(.select(2), .width(32), .enable("false")) multiplexer_3 (
    .in0(RAM_Out_0), .in1(RAM_Out_1), .in2(RAM_Out_2), .in3(RAM_Out_3), .out(multiplexer_3_out), .sel(offset));
  Demultiplexer #(.select(2), .width(32), .enable("false")) demultiplexer_1 (
    .out0(RAM_In_0), .out1(RAM_In_1), .out2(RAM_In_2), .out3(RAM_In_3), .in(little_endian_1_output),
    .sel(offset));
  Control_Unit_2 control_unit_1 (
    .END_CS_IN(END_CS), .RST(Reset), .CLK(Clock), .Func_Code(func_code), .OP_Code(op_code), .Flag(flag),
    .ALUB(control_unit_1_alub), .out_7(control_unit_1_out_7), .CS(CS_In), .TTY_ENABLE(TTY_Enable),
    .ALU_SEL(control_unit_1_alu_sel), .ALUA(control_unit_1_alua), .RFInput(control_unit_1_rfinput),
    .RF_SEL(control_unit_1_rf_sel), .BCSelector(control_unit_1_bcselector),
    .FlagSelector(control_unit_1_flagselector), .writeRF(control_unit_1_writerf),
    .writePC(control_unit_1_writepc), .\unsigned (control_unit_1_unsigned), .MA_SEL(MA_SEL),
    .DOut_SEL(control_unit_1_dout_sel), .RAM_RW(RAM_RW_In), .DIn_SEL(DIn_SEL), .KBD_EN(Kbd_Enable),
    .halt(Stop));
  Little_Endian little_endian_2 (.Input(multiplexer_3_out), .Output(RAM_Output));

  assign Kbd_Clear = Reset;

  // Other names for the same wires on the sheet: KBD_DATA[6:0] = Kbd_ASCII_Data; CLK = Clock; CS = Chip_Select;
  //   KBD_AVAIL = Kbd_Available; CLR = Reset; KBD_CLR = Reset; RAM_A[15:0] = Address; RAM_INPUT_0[31:0] = RAM_In_0;
  //   RAM_INPUT_1[31:0] = RAM_In_1; RAM_INPUT_2[31:0] = RAM_In_2; RAM_INPUT_3[31:0] = RAM_In_3; RAM_MASK[3:0] = Mask;
  //   RAM_OUTPUT_0[31:0] = RAM_Out_0; RAM_OUTPUT_1[31:0] = RAM_Out_1; RAM_OUTPUT_2[31:0] = RAM_Out_2;
  //   RAM_OUTPUT_3[31:0] = RAM_Out_3; RW = nRead_Write; TTY_DATA[6:0] = TTY_ASCII_Data

  // Notes on the sheet:
  //   RAM ADDRESS
  //   DATA FROM RAM
  //   DATA TO RAM
  //   DATA WRITE MASK
  //   RAM TIMING
  //   RAM CONTROL
  //   KEYBOARD
  //   TTY
  //   SEQUENCING
endmodule

module RAM_Dispatcher (
  input  [3:0] WriteTime,
  input  Clock,
  input  CLR,
  output [31:0] Data,
  output [15:0] Address,
  output [3:0] Mask,
  output Finished,
  output Write
);

  wire demultiplexer_2_out1, demultiplexer_3_out1, End, IDLE_q, IncAddr, Load, or_1_out, or_2_out, While_q,
       WriteEnd;
  wire [3:0] counter_1_q;
  wire [31:0] CurrentAddress_q;

  Counter #(.width(32), .max('hffffffff)) CurrentAddress (
    .count(IncAddr), .Q({CurrentAddress_q[31:18], Address, CurrentAddress_q[1:0]}), .clk(Clock), .clr(CLR));  // open: load, D, carry
  or or_1 (or_1_out, IncAddr, demultiplexer_3_out1, Finished);
  D_Flip_Flop IDLE (.clk(Clock), .D(or_1_out), .Q(IDLE_q), .preset(CLR));  // open: Qn, en, reset
  Demultiplexer #(.enable("false")) demultiplexer_1 (.out0(Load), .out1(Finished), .in(IDLE_q), .sel(End));
  D_Flip_Flop While (.clk(Clock), .D(or_2_out), .Q(While_q), .reset(CLR));  // open: Qn, preset, en
  or or_2 (or_2_out, Write, Load);
  RAM_part #(.addrWidth(18), .dataWidth(32)) ram_1 (
    .addr({Address, CurrentAddress_q[1:0]}), .data(Data), .clk(Clock));  // open: sel, ld, clr
  Demultiplexer #(.enable("false")) demultiplexer_2 (
    .out0(Write), .out1(demultiplexer_2_out1), .in(While_q), .sel(WriteEnd));
  Decoder #(.select(2)) decoder_1 (
    .out0(Mask[0]), .out1(Mask[1]), .out2(Mask[2]), .out3(Mask[3]), .sel(CurrentAddress_q[1:0]));  // open: en
  Demultiplexer #(.enable("false")) demultiplexer_3 (
    .out0(IncAddr), .out1(demultiplexer_3_out1), .in(demultiplexer_2_out1), .sel(End));
  Counter #(.width(4), .max('hf)) counter_1 (
    .load(Load), .D(WriteTime), .count(Write), .Q(counter_1_q), .clk(Clock));  // open: carry, clr
  Comparator #(.width(32)) comparator_1 (.a(Data), .b({32{1'b1}}), .eq(End));  // open: gt, lt
  Comparator #(.width(4)) comparator_2 (.a(4'b0000), .b(counter_1_q), .eq(WriteEnd));  // open: gt, lt

  // Other names for the same wires on the sheet: CLK = Clock; Count = Write; WT[3:0] = WriteTime
endmodule

module Little_Endian (
  input  [31:0] Input,
  output [31:0] Output
);


  assign Output = {Input[7:0], Input[15:8], Input[23:16], Input[31:24]};
endmodule

module RAMRW (
  input  [3:0] Read_Time,
  input  [3:0] Write_Time,
  input  in_3,
  input  in_4,
  input  CS_In,
  input  RWSrc,
  output END,
  output CS,
  output RW
);

  wire comparator_1_gt, comparator_2_gt, CountRT, demultiplexer_1_out0, demultiplexer_1_out1,
       demultiplexer_2_out0, demultiplexer_2_out1, demultiplexer_3_out0, demultiplexer_3_out1, end_t,
       not_3_out, not_4_out, or_2_out, or_3_out, RST, RTcontinue, WTcontinue;
  wire [3:0] counter_1_q, counter_2_q;

  Counter #(.width(4), .max('hf)) counter_1 (
    .count(CountRT), .Q(counter_1_q), .clk(in_3), .clr(RST));  // open: load, D, carry
  Counter #(.width(4), .max('hf)) counter_2 (
    .count(RW), .Q(counter_2_q), .clk(in_3), .clr(RST));  // open: load, D, carry
  Comparator #(.width(4)) comparator_1 (.a(Read_Time), .b(counter_1_q), .gt(comparator_1_gt));  // open: eq, lt
  or or_1 (RST, in_4, end_t);
  not not_1 (RTcontinue, comparator_1_gt);
  not not_2 (WTcontinue, comparator_2_gt);
  Comparator #(.width(4)) comparator_2 (.a(Write_Time), .b(counter_2_q), .gt(comparator_2_gt));  // open: eq, lt
  Demultiplexer #(.enable("false")) demultiplexer_1 (
    .out0(demultiplexer_1_out0), .out1(demultiplexer_1_out1), .in(CS_In), .sel(RWSrc));
  not not_3 (not_3_out, RTcontinue);
  Demultiplexer #(.enable("false")) demultiplexer_2 (
    .out0(demultiplexer_2_out0), .out1(demultiplexer_2_out1), .in(or_2_out), .sel(not_3_out));
  or or_2 (or_2_out, demultiplexer_1_out0, CountRT);
  not not_4 (not_4_out, WTcontinue);
  Demultiplexer #(.enable("false")) demultiplexer_3 (
    .out0(demultiplexer_3_out0), .out1(demultiplexer_3_out1), .in(or_3_out), .sel(not_4_out));
  or or_3 (or_3_out, demultiplexer_1_out1, RW);
  D_Flip_Flop d_ff_1 (.clk(in_3), .D(demultiplexer_2_out1), .Q(CountRT), .reset(RST));  // open: Qn, preset, en
  D_Flip_Flop d_ff_2 (.clk(in_3), .D(demultiplexer_3_out1), .Q(RW), .reset(RST));  // open: Qn, preset, en
  or or_4 (END, demultiplexer_2_out0, demultiplexer_3_out0);
  D_Flip_Flop d_ff_3 (.clk(in_3), .D(END), .Q(end_t), .reset(RST));  // open: Qn, preset, en
  or or_5 (CS, CountRT, RW);

  // Other names for the same wires on the sheet: Clk = in_3; CS0 = CountRT; CountWT = RW; CS1 = RW; reset = in_4;
  //   RT[3:0] = Read_Time; WT[3:0] = Write_Time
endmodule

module ABS (
  input  [31:0] in_1,
  input  in_2,
  output [31:0] out_3,
  output out_4
);

  wire bitselector_1_out;
  wire [31:0] negator_1_out;

  BitSelector #(.width(32)) bitselector_1 (.in(in_1), .out(bitselector_1_out), .sel({5{1'b1}}));
  Negator #(.width(32)) negator_1 (.in(in_1), .out(negator_1_out));
  and and_1 (out_4, ~in_2, bitselector_1_out);  // AND_Gate
  Multiplexer #(.width(32), .enable("false")) multiplexer_1 (.in0(in_1), .in1(negator_1_out), .out(out_3), .sel(out_4));

  // Other names for the same wires on the sheet: Input[31:0] = in_1

  // Notes on the sheet:
  //   Absolute Value
endmodule

module Multi (
  input  [31:0] in_1,
  input  [31:0] in_2,
  input  in_3,
  output [31:0] out_4,
  output [31:0] out_5
);

  wire adder_1_cout, sign, SIGN_A, SIGN_B, xor_1_out;
  wire [31:0] ABS_A, ABS_B, ABS_HI, ABS_LO, bit_extender_1_out, not_1_out, not_2_out, sHI, sLO;

  ABS abs_1 (.in_1(in_1), .in_2(in_3), .out_3(ABS_A), .out_4(SIGN_A));
  ABS abs_2 (.in_1(in_2), .in_2(in_3), .out_3(ABS_B), .out_4(SIGN_B));
  xor xor_1 (xor_1_out, SIGN_A, SIGN_B);
  and and_1 (sign, xor_1_out, ~in_3);  // AND_Gate
  Multiplier #(.width(32)) multiplier_1 (.a(ABS_A), .b(ABS_B), .out(ABS_LO), .cout(ABS_HI));  // open: cin
  assign not_1_out = ~ABS_LO;  // NOT_Gate not_1, 32 bits wide
  assign not_2_out = ~ABS_HI;  // NOT_Gate not_2, 32 bits wide
  Adder #(.width(32)) adder_1 (.a(not_1_out), .b(32'h1), .out(sLO), .cout(adder_1_cout));  // open: cin
  assign bit_extender_1_out = {{31{1'b0}}, adder_1_cout};  // Bit_Extender bit_extender_1
  Adder #(.width(32)) adder_2 (.a(bit_extender_1_out), .b(not_2_out), .out(sHI));  // open: cin, cout
  Multiplexer #(.width(32), .enable("false")) multiplexer_1 (.in0(ABS_HI), .in1(sHI), .out(out_4), .sel(sign));
  Multiplexer #(.width(32), .enable("false")) multiplexer_2 (.in0(ABS_LO), .in1(sLO), .out(out_5), .sel(sign));

  // Other names for the same wires on the sheet: A[31:0] = in_1; B[31:0] = in_2; HI[31:0] = out_4; LO[31:0] = out_5;
  //   unsigned = in_3

  // Notes on the sheet:
  //   Multiplier
  //   UNSIGNED-SIGNED
endmodule

module Div (
  input  [31:0] in_1,
  input  [31:0] in_2,
  input  in_3,
  output [31:0] Cocient,
  output [31:0] Remainder
);

  wire and_1_out, and_2_out, sign, xor_1_out;
  wire [31:0] C, multiplexer_1_out, multiplexer_2_out, negator_1_out, negator_2_out, negator_3_out;

  xor xor_1 (xor_1_out, in_1[31], in_2[31]);
  Negator #(.width(32)) negator_1 (.in(in_1), .out(negator_1_out));
  and and_1 (and_1_out, in_1[31], ~in_3);  // AND_Gate
  and and_2 (and_2_out, ~in_3, in_2[31]);  // AND_Gate
  Negator #(.width(32)) negator_2 (.in(in_2), .out(negator_2_out));
  and and_3 (sign, xor_1_out, ~in_3);  // AND_Gate
  Multiplexer #(.width(32), .enable("false")) multiplexer_1 (
    .in0(in_1), .in1(negator_1_out), .out(multiplexer_1_out), .sel(and_1_out));
  Multiplexer #(.width(32), .enable("false")) multiplexer_2 (
    .in0(in_2), .in1(negator_2_out), .out(multiplexer_2_out), .sel(and_2_out));
  Divider #(.width(32)) divider_1 (
    .a(multiplexer_1_out), .b(multiplexer_2_out), .out(C), .rem(Remainder));  // open: upper
  Negator #(.width(32)) negator_3 (.in(C), .out(negator_3_out));
  Multiplexer #(.width(32), .enable("false")) multiplexer_3 (.in0(C), .in1(negator_3_out), .out(Cocient), .sel(sign));

  // Other names for the same wires on the sheet: A[31:0] = in_1; signA = in_1[31]; B[31:0] = in_2; signB = in_2[31];
  //   R[31:0] = Remainder; unsigned = in_3

  // Notes on the sheet:
  //   DIVIDER
  //   (UNSIGNED-SIGNED)
endmodule

module ALU_2 (
  input  [31:0] in_1,
  input  in_2,
  input  [3:0] in_3,
  input  [31:0] in_4,
  output out_5,
  output [31:0] out_6,
  output out_7,
  output [31:0] out_8,
  output Mul_Div,
  output [31:0] out_10,
  output out_11,
  output out_12,
  output out_13
);

  wire [0:0] lt, ltu;
  wire [31:0] add, \and , C, multHI, multLO, \nor , \or , R, sub, \xor ;

  assign \and  = in_1 & in_4;  // AND_Gate and_1, 32 bits wide
  assign \or  = in_1 | in_4;  // OR_Gate or_1, 32 bits wide
  assign \xor  = in_1 ^ in_4;  // XOR_Gate xor_1, 32 bits wide
  Comparator #(.width(32), .mode("unsigned")) comparator_1 (.a(in_1), .b(in_4), .eq(out_7), .lt(ltu[0]));  // open: gt
  assign \nor  = ~(in_1 | in_4);  // NOR_Gate nor_1, 32 bits wide
  Multiplexer #(.width(32), .enable("false")) multiplexer_1 (.in0(multHI), .in1(R), .out(out_6), .sel(in_3[0]));
  Multiplexer #(.width(32), .enable("false")) multiplexer_2 (.in0(multLO), .in1(C), .out(out_10), .sel(in_3[0]));
  Multi multi_1 (.in_1(in_1), .in_2(in_4), .in_3(in_2), .out_4(multHI), .out_5(multLO));
  Div div_1 (.in_1(in_1), .in_2(in_4), .in_3(in_2), .Cocient(C), .Remainder(R));
  Adder #(.width(32)) adder_1 (.a(in_1), .b(in_4), .out(add));  // open: cin, cout
  Subtractor #(.width(32)) subtractor_1 (.a(in_1), .b(in_4), .out(sub));  // open: bin, bout
  Comparator #(.width(32)) comparator_2 (.a(in_1), .b(in_4), .eq(out_7), .lt(lt[0]));  // open: gt
  not not_1 (out_11, out_12);
  Comparator #(.width(32)) comparator_3 (.a(in_1), .b({32{1'b0}}), .gt(out_12), .lt(out_13));  // open: eq
  Multiplexer #(.select(4), .width(32), .enable("false")) multiplexer_3 (
    .in0(add), .in1(sub), .in4(\and ), .in5(\or ), .in6(\nor ), .in7(\xor ), .in8({{31{1'b0}}, lt[0]}),
    .in9({{31{1'b0}}, ltu[0]}), .out(out_8), .sel(in_3));  // open: in2, in3, in10, in11, in12, in13, in14, in15
  // Probe on in_1
  // Probe on in_4
  not not_2 (out_5, out_7);
  and and_2 (Mul_Div, in_3[1], ~in_3[2], ~in_3[3]);  // AND_Gate
  // Probe on out_6
  // Probe on R
  // Probe on out_10

  // Other names for the same wires on the sheet: A[31:0] = in_1; B[31:0] = in_4; equ = out_7; gtz = out_12;
  //   HI[31:0] = out_6; letz = out_11; LO[31:0] = out_10; ltz = out_13; RES[31:0] = out_8; select[3:0] = in_3;
  //   unsigned = in_2

  // Notes on the sheet:
  //   Logic
  //   Operators
  //   ALU
  //   Aritmetic
  //   Outputs
  //   Flags
endmodule

module _32_bit_Register (
  input  CLK,
  input  RST,
  input  Load,
  input  [31:0] Data_In,
  output [31:0] out_5
);

  wire undriven, undriven_2, undriven_3, undriven_4, undriven_5, undriven_6, undriven_7, undriven_8,
       undriven_9, undriven_10, undriven_11, undriven_12, undriven_13, undriven_14, undriven_15, undriven_16,
       undriven_17, undriven_18, undriven_19, undriven_20, undriven_21, undriven_22, undriven_23,
       undriven_24, undriven_25, undriven_26, undriven_27, undriven_28, undriven_29, undriven_30,
       undriven_31, undriven_32;

  D_Flip_Flop d_ff_1 (.clk(CLK), .D(Data_In[0]), .Q(out_5[0]), .preset(undriven), .en(Load), .reset(RST));  // open: Qn
  D_Flip_Flop d_ff_2 (
    .clk(CLK), .D(Data_In[1]), .Q(out_5[1]), .preset(undriven_2), .en(Load), .reset(RST));  // open: Qn
  D_Flip_Flop d_ff_3 (
    .clk(CLK), .D(Data_In[2]), .Q(out_5[2]), .preset(undriven_3), .en(Load), .reset(RST));  // open: Qn
  D_Flip_Flop d_ff_4 (
    .clk(CLK), .D(Data_In[3]), .Q(out_5[3]), .preset(undriven_4), .en(Load), .reset(RST));  // open: Qn
  D_Flip_Flop d_ff_5 (
    .clk(CLK), .D(Data_In[4]), .Q(out_5[4]), .preset(undriven_5), .en(Load), .reset(RST));  // open: Qn
  D_Flip_Flop d_ff_6 (
    .clk(CLK), .D(Data_In[5]), .Q(out_5[5]), .preset(undriven_6), .en(Load), .reset(RST));  // open: Qn
  D_Flip_Flop d_ff_7 (
    .clk(CLK), .D(Data_In[6]), .Q(out_5[6]), .preset(undriven_7), .en(Load), .reset(RST));  // open: Qn
  D_Flip_Flop d_ff_8 (
    .clk(CLK), .D(Data_In[7]), .Q(out_5[7]), .preset(undriven_8), .en(Load), .reset(RST));  // open: Qn
  D_Flip_Flop d_ff_9 (
    .clk(CLK), .D(Data_In[8]), .Q(out_5[8]), .preset(undriven_9), .en(Load), .reset(RST));  // open: Qn
  D_Flip_Flop d_ff_10 (
    .clk(CLK), .D(Data_In[9]), .Q(out_5[9]), .preset(undriven_10), .en(Load), .reset(RST));  // open: Qn
  D_Flip_Flop d_ff_11 (
    .clk(CLK), .D(Data_In[10]), .Q(out_5[10]), .preset(undriven_11), .en(Load), .reset(RST));  // open: Qn
  D_Flip_Flop d_ff_12 (
    .clk(CLK), .D(Data_In[11]), .Q(out_5[11]), .preset(undriven_12), .en(Load), .reset(RST));  // open: Qn
  D_Flip_Flop d_ff_13 (
    .clk(CLK), .D(Data_In[12]), .Q(out_5[12]), .preset(undriven_13), .en(Load), .reset(RST));  // open: Qn
  D_Flip_Flop d_ff_14 (
    .clk(CLK), .D(Data_In[13]), .Q(out_5[13]), .preset(undriven_14), .en(Load), .reset(RST));  // open: Qn
  D_Flip_Flop d_ff_15 (
    .clk(CLK), .D(Data_In[14]), .Q(out_5[14]), .preset(undriven_15), .en(Load), .reset(RST));  // open: Qn
  D_Flip_Flop d_ff_16 (
    .clk(CLK), .D(Data_In[15]), .Q(out_5[15]), .preset(undriven_16), .en(Load), .reset(RST));  // open: Qn
  D_Flip_Flop d_ff_17 (
    .clk(CLK), .D(Data_In[16]), .Q(out_5[16]), .preset(undriven_17), .en(Load), .reset(RST));  // open: Qn
  D_Flip_Flop d_ff_18 (
    .clk(CLK), .D(Data_In[17]), .Q(out_5[17]), .preset(undriven_18), .en(Load), .reset(RST));  // open: Qn
  D_Flip_Flop d_ff_19 (
    .clk(CLK), .D(Data_In[18]), .Q(out_5[18]), .preset(undriven_19), .en(Load), .reset(RST));  // open: Qn
  D_Flip_Flop d_ff_20 (
    .clk(CLK), .D(Data_In[19]), .Q(out_5[19]), .preset(undriven_20), .en(Load), .reset(RST));  // open: Qn
  D_Flip_Flop d_ff_21 (
    .clk(CLK), .D(Data_In[20]), .Q(out_5[20]), .preset(undriven_21), .en(Load), .reset(RST));  // open: Qn
  D_Flip_Flop d_ff_22 (
    .clk(CLK), .D(Data_In[21]), .Q(out_5[21]), .preset(undriven_22), .en(Load), .reset(RST));  // open: Qn
  D_Flip_Flop d_ff_23 (
    .clk(CLK), .D(Data_In[22]), .Q(out_5[22]), .preset(undriven_23), .en(Load), .reset(RST));  // open: Qn
  D_Flip_Flop d_ff_24 (
    .clk(CLK), .D(Data_In[23]), .Q(out_5[23]), .preset(undriven_24), .en(Load), .reset(RST));  // open: Qn
  D_Flip_Flop d_ff_25 (
    .clk(CLK), .D(Data_In[24]), .Q(out_5[24]), .preset(undriven_25), .en(Load), .reset(RST));  // open: Qn
  D_Flip_Flop d_ff_26 (
    .clk(CLK), .D(Data_In[25]), .Q(out_5[25]), .preset(undriven_26), .en(Load), .reset(RST));  // open: Qn
  D_Flip_Flop d_ff_27 (
    .clk(CLK), .D(Data_In[26]), .Q(out_5[26]), .preset(undriven_27), .en(Load), .reset(RST));  // open: Qn
  D_Flip_Flop d_ff_28 (
    .clk(CLK), .D(Data_In[27]), .Q(out_5[27]), .preset(undriven_28), .en(Load), .reset(RST));  // open: Qn
  D_Flip_Flop d_ff_29 (
    .clk(CLK), .D(Data_In[28]), .Q(out_5[28]), .preset(undriven_29), .en(Load), .reset(RST));  // open: Qn
  D_Flip_Flop d_ff_30 (
    .clk(CLK), .D(Data_In[29]), .Q(out_5[29]), .preset(undriven_30), .en(Load), .reset(RST));  // open: Qn
  D_Flip_Flop d_ff_31 (
    .clk(CLK), .D(Data_In[30]), .Q(out_5[30]), .preset(undriven_31), .en(Load), .reset(RST));  // open: Qn
  D_Flip_Flop d_ff_32 (
    .clk(CLK), .D(Data_In[31]), .Q(out_5[31]), .preset(undriven_32), .en(Load), .reset(RST));  // open: Qn

  // Other names for the same wires on the sheet: i0[7:0] = Data_In[7:0]; i1[7:0] = Data_In[15:8];
  //   i2[7:0] = Data_In[23:16]; i3[7:0] = Data_In[31:24]; en = Load; o0[7:0] = out_5[7:0]; o1[7:0] = out_5[15:8];
  //   o2[7:0] = out_5[23:16]; o3[7:0] = out_5[31:24]
endmodule

module _32x32_RF (
  input  Reset,
  input  [31:0] WriteData,
  input  [4:0] WriteReg,
  input  [4:0] ReadReg1,
  input  [4:0] ReadReg2,
  input  RegWriteEnable,
  input  CLK,
  input  [31:0] Hi,
  input  [31:0] Lo,
  input  mult_div,
  output [31:0] ReadData1,
  output [31:0] ReadData2,
  output [31:0] OutHi,
  output [31:0] OutLo,
  output [31:0] SP
);

  wire L0, L1, L2, L3, L4, L5, L6, L7, L8, L9, L10, L11, L12, L13, L14, L15, L16, L17, L18, L19, L20, L21,
       L22, L23, L24, L25, L26, L27, L28, L29, L30, L31;
  wire [31:0] o0, o1, o2, o3, o4, o5, o6, o7, o8, o9, o10, o11, o12, o13, o14, o15, o16, o17, o18, o19, o20,
       o21, o22, o23, o24, o25, o26, o27, o28, o29, o30;

  _32_bit_Register u_32_bit_register_1 (.CLK(CLK), .RST(Reset), .Load(L0), .Data_In(WriteData), .out_5(o0));
  _32_bit_Register u_32_bit_register_2 (.CLK(CLK), .RST(Reset), .Load(L8), .Data_In(WriteData), .out_5(o8));
  _32_bit_Register u_32_bit_register_3 (.CLK(CLK), .RST(Reset), .Load(L16), .Data_In(WriteData), .out_5(o16));
  _32_bit_Register u_32_bit_register_4 (.CLK(CLK), .RST(Reset), .Load(L24), .Data_In(WriteData), .out_5(o24));
  Demultiplexer #(.select(5)) demultiplexer_1 (
    .out0(L0), .out1(L1), .out2(L2), .out3(L3), .out4(L4), .out5(L5), .out6(L6), .out7(L7), .out8(L8),
    .out9(L9), .out10(L10), .out11(L11), .out12(L12), .out13(L13), .out14(L14), .out15(L15), .out16(L16),
    .out17(L17), .out18(L18), .out19(L19), .out20(L20), .out21(L21), .out22(L22), .out23(L23), .out24(L24),
    .out25(L25), .out26(L26), .out27(L27), .out28(L28), .out29(L29), .out30(L30), .out31(L31),
    .in(RegWriteEnable), .sel(WriteReg));  // open: en
  _32_bit_Register u_32_bit_register_5 (.CLK(CLK), .RST(Reset), .Load(L1), .Data_In(WriteData), .out_5(o1));
  _32_bit_Register u_32_bit_register_6 (.CLK(CLK), .RST(Reset), .Load(L9), .Data_In(WriteData), .out_5(o9));
  _32_bit_Register u_32_bit_register_7 (.CLK(CLK), .RST(Reset), .Load(L17), .Data_In(WriteData), .out_5(o17));
  _32_bit_Register u_32_bit_register_8 (.CLK(CLK), .RST(Reset), .Load(L25), .Data_In(WriteData), .out_5(o25));
  _32_bit_Register u_32_bit_register_9 (.CLK(CLK), .RST(Reset), .Load(L2), .Data_In(WriteData), .out_5(o2));
  _32_bit_Register u_32_bit_register_10 (.CLK(CLK), .RST(Reset), .Load(L10), .Data_In(WriteData), .out_5(o10));
  _32_bit_Register u_32_bit_register_11 (.CLK(CLK), .RST(Reset), .Load(L18), .Data_In(WriteData), .out_5(o18));
  _32_bit_Register u_32_bit_register_12 (.CLK(CLK), .RST(Reset), .Load(L26), .Data_In(WriteData), .out_5(o26));
  _32_bit_Register u_32_bit_register_13 (.CLK(CLK), .RST(Reset), .Load(L3), .Data_In(WriteData), .out_5(o3));
  _32_bit_Register u_32_bit_register_14 (.CLK(CLK), .RST(Reset), .Load(L11), .Data_In(WriteData), .out_5(o11));
  _32_bit_Register u_32_bit_register_15 (.CLK(CLK), .RST(Reset), .Load(L19), .Data_In(WriteData), .out_5(o19));
  _32_bit_Register u_32_bit_register_16 (.CLK(CLK), .RST(Reset), .Load(L27), .Data_In(WriteData), .out_5(o27));
  Multiplexer #(.select(5), .width(32), .enable("false")) multiplexer_1 (
    .in0(o0), .in1(o1), .in2(o2), .in3(o3), .in4(o4), .in5(o5), .in6(o6), .in7(o7), .in8(o8), .in9(o9),
    .in10(o10), .in11(o11), .in12(o12), .in13(o13), .in14(o14), .in15(o15), .in16(o16), .in17(o17),
    .in18(o18), .in19(o19), .in20(o20), .in21(o21), .in22(o22), .in23(o23), .in24(o24), .in25(o25),
    .in26(o26), .in27(o27), .in28(o28), .in29(o29), .in30(o30), .in31(SP), .out(ReadData1), .sel(ReadReg1));
  _32_bit_Register u_32_bit_register_17 (.CLK(CLK), .RST(Reset), .Load(L4), .Data_In(WriteData), .out_5(o4));
  _32_bit_Register u_32_bit_register_18 (.CLK(CLK), .RST(Reset), .Load(L12), .Data_In(WriteData), .out_5(o12));
  _32_bit_Register u_32_bit_register_19 (.CLK(CLK), .RST(Reset), .Load(L20), .Data_In(WriteData), .out_5(o20));
  _32_bit_Register u_32_bit_register_20 (.CLK(CLK), .RST(Reset), .Load(L28), .Data_In(WriteData), .out_5(o28));
  Multiplexer #(.select(5), .width(32), .enable("false")) multiplexer_2 (
    .in0(o0), .in1(o1), .in2(o2), .in3(o3), .in4(o4), .in5(o5), .in6(o6), .in7(o7), .in8(o8), .in9(o9),
    .in10(o10), .in11(o11), .in12(o12), .in13(o13), .in14(o14), .in15(o15), .in16(o16), .in17(o17),
    .in18(o18), .in19(o19), .in20(o20), .in21(o21), .in22(o22), .in23(o23), .in24(o24), .in25(o25),
    .in26(o26), .in27(o27), .in28(o28), .in29(o29), .in30(o30), .in31(SP), .out(ReadData2), .sel(ReadReg2));
  _32_bit_Register u_32_bit_register_21 (.CLK(CLK), .RST(Reset), .Load(L5), .Data_In(WriteData), .out_5(o5));
  _32_bit_Register u_32_bit_register_22 (.CLK(CLK), .RST(Reset), .Load(L13), .Data_In(WriteData), .out_5(o13));
  _32_bit_Register u_32_bit_register_23 (.CLK(CLK), .RST(Reset), .Load(L21), .Data_In(WriteData), .out_5(o21));
  _32_bit_Register u_32_bit_register_24 (.CLK(CLK), .RST(Reset), .Load(L29), .Data_In(WriteData), .out_5(o29));
  _32_bit_Register u_32_bit_register_25 (.CLK(CLK), .RST(Reset), .Load(L6), .Data_In(WriteData), .out_5(o6));
  _32_bit_Register u_32_bit_register_26 (.CLK(CLK), .RST(Reset), .Load(L14), .Data_In(WriteData), .out_5(o14));
  _32_bit_Register u_32_bit_register_27 (.CLK(CLK), .RST(Reset), .Load(L22), .Data_In(WriteData), .out_5(o22));
  _32_bit_Register u_32_bit_register_28 (.CLK(CLK), .RST(Reset), .Load(L30), .Data_In(WriteData), .out_5(o30));
  _32_bit_Register u_32_bit_register_29 (.CLK(CLK), .RST(Reset), .Load(mult_div), .Data_In(Hi), .out_5(OutHi));
  _32_bit_Register u_32_bit_register_30 (.CLK(CLK), .RST(Reset), .Load(mult_div), .Data_In(Lo), .out_5(OutLo));
  _32_bit_Register u_32_bit_register_31 (.CLK(CLK), .RST(Reset), .Load(L7), .Data_In(WriteData), .out_5(o7));
  _32_bit_Register u_32_bit_register_32 (.CLK(CLK), .RST(Reset), .Load(L15), .Data_In(WriteData), .out_5(o15));
  _32_bit_Register u_32_bit_register_33 (.CLK(CLK), .RST(Reset), .Load(L23), .Data_In(WriteData), .out_5(o23));
  _32_bit_Register u_32_bit_register_34 (.CLK(CLK), .RST(Reset), .Load(L31), .Data_In(WriteData), .out_5(SP));

  // Other names for the same wires on the sheet: A1[4:0] = ReadReg1; A2[4:0] = ReadReg2; A3[4:0] = WriteReg;
  //   o31[31:0] = SP; RD1[31:0] = ReadData1; RD2[31:0] = ReadData2; RW = RegWriteEnable; WD[31:0] = WriteData

  // Notes on the sheet:
  //   R0
  //   R8
  //   R16
  //   R24
  //        R1
  //   R9
  //   R17
  //   R25
  //   R2
  //   R10
  //   R18
  //   R26
  //   R3
  //   R11
  //   R19
  //   R27
  //   R4
  //   R12
  //   R20
  //   R28
  //   R5
  //   R13
  //   R21
  //   R29
  //   R6
  //   R14
  //   R22
  //   R30
  //   R7
  //   R15
  //   R23
  //   R31
endmodule

module Control_Unit_2 (
  input  END_CS_IN,
  input  RST,
  input  CLK,
  input  [5:0] Func_Code,
  input  [5:0] OP_Code,
  input  Flag,
  output out_7,
  output CS,
  output TTY_ENABLE,
  output [3:0] ALU_SEL,
  output [1:0] ALUB,
  output ALUA,
  output [2:0] RFInput,
  output [1:0] RF_SEL,
  output [1:0] BCSelector,
  output [2:0] FlagSelector,
  output writeRF,
  output writePC,
  output \unsigned ,
  output [1:0] MA_SEL,
  output DOut_SEL,
  output RAM_RW,
  output DIn_SEL,
  output KBD_EN,
  output halt
);

  wire _1_Cycle_q, add, addi, ALUA_pop, ALUA_SEL_Imm, ALUA_stack, \and , andi, beq, bgtz, blez, bltz, bne,
       branch, BranchEnd, CS_EN_Instruction, CS_EN_pop, CS_EN_push, CS_EN_stack, demultiplexer_1_out1,
       demultiplexer_2_out0, demultiplexer_3_out1, demultiplexer_4_out0, demultiplexer_5_out0,
       demultiplexer_5_out1, demultiplexer_6_out0, demultiplexer_6_out1, demultiplexer_7_out1,
       demultiplexer_8_out0, demultiplexer_8_out1, demultiplexer_11_out1, div, divu, halt_t, IDLE_q,
       immediate, ImmEnd, jmp, jmpEnd, jr, load_Word, LoadEnd, mfhi, mflo, mul, mulu, next, nop, \nor ,
       not_1_out, not_2_out, not_3_out, not_4_out, not_5_out, \or , or_1_out, or_2_out, or_3_out, or_4_out,
       or_6_out, or_8_out, or_9_out, or_17_out, ori, push_tty, rnd, slt, slti, sltiu, sltu, special,
       SpecialEnd, stack, StackEnd, stBranch, stImm, stLoad_Word, store_Word, StoreEnd, stSpecial, stStack,
       stStore_Word, stZero, sub, WAIT_READ_2_q, WAIT_READ_q, WRITE_RF_Imm, WRITE_RF_Zero, WritePC_Imm,
       WritePC_stack, WritePC_Store, WritePC_Zero, WRTE_RF_stack, \xor , xori, zero, ZeroEnd;
  wire [0:0] ALU_SEL_push, ALUB_SEL_Load, BC_SEL_Branch, RF_Input_pop, RF_SEL_Load;
  wire [1:0] ALUB_SEL_Imm, ALUB_stack, BC_SEL_Imm, BC_SEL_Zero, MA_SEL_stack, RF_SEL_Imm, RF_SEL_Zero;
  wire [1:1] BC_SEL_Jmp, RF_SEL_rnd_kbd;
  wire [2:0] RF_Input_Imm, RF_Input_Zero;
  wire [2:2] RF_Input_rnd;
  wire [3:0] ALU_SEL_Imm, ALU_SEL_Zero;

  Branch_Mapper branch_mapper_1 (.BEQ(beq), .BNE(bne), .BLEZ(blez), .BGTZ(bgtz), .BLTZ(bltz), .Flag_Sel(FlagSelector));
  Demultiplexer demultiplexer_1 (
    .out0(WritePC_Store), .out1(demultiplexer_1_out1), .in(or_1_out), .sel(not_1_out));  // open: en
  or or_1 (or_1_out, stStore_Word, DOut_SEL);
  Demultiplexer demultiplexer_2 (
    .out0(demultiplexer_2_out0), .out1(ALU_SEL_push[0]), .in(stStack), .sel(push_tty));  // open: en
  Op_Code_Decoder op_code_decoder_1 (
    .o1(OP_Code[0]), .o2(OP_Code[1]), .o3(OP_Code[2]), .o4(OP_Code[3]), .o5(OP_Code[4]), .o6(OP_Code[5]),
    .enable(1'b1), .ZERO(zero), .XORi(xori), .STACK(stack), .ADDi(addi), .SLTi(slti), .SPECIAL(special),
    .ANDi(andi), .SLTiU(sltiu), .JUMP(jmp), .ORi(ori), .BEQ(beq), .BLTZ(bltz), .BNE(bne), .LW(load_Word),
    .BLEZ(blez), .SW(store_Word), .BGTZ(bgtz));
  Func_Code_Decoder func_code_decoder_1 (
    .f1(Func_Code[0]), .f2(Func_Code[1]), .f3(Func_Code[2]), .f4(Func_Code[3]), .f5(Func_Code[4]),
    .f6(Func_Code[5]), .enable(1'b1), .AND(\and ), .ADD(add), .DIV(div), .NOP_POP(nop), .RND(rnd), .OR(\or ),
    .SUB(sub), .DIVU(divu), .PUSH_TTY(push_tty), .XOR(\xor ), .MUL(mul), .SLT(slt), .HALT(halt_t),
    .NOR(\nor ), .MULU(mulu), .SLTU(sltu), .MFHI(mfhi), .MFLO(mflo), .JR(jr));  // open: KBD
  not not_1 (not_1_out, END_CS_IN);
  Demultiplexer demultiplexer_3 (
    .out0(RF_Input_pop[0]), .out1(demultiplexer_3_out1), .in(or_2_out), .sel(not_2_out));  // open: en
  or or_2 (or_2_out, demultiplexer_2_out0, CS_EN_pop);
  not not_2 (not_2_out, END_CS_IN);
  Demultiplexer demultiplexer_4 (
    .out0(demultiplexer_4_out0), .out1(BC_SEL_Branch[0]), .in(stBranch), .sel(Flag));  // open: en
  D_Flip_Flop WAIT (.clk(CLK), .D(demultiplexer_1_out1), .Q(DOut_SEL), .reset(RST));  // open: Qn, preset, en
  D_Flip_Flop _1_Cycle (.clk(CLK), .D(ALU_SEL_push[0]), .Q(_1_Cycle_q), .reset(RST));  // open: Qn, preset, en
  D_Flip_Flop IDLE (.clk(CLK), .D(demultiplexer_5_out1), .Q(IDLE_q), .preset(RST));  // open: Qn, en, reset
  Demultiplexer demultiplexer_5 (
    .out0(demultiplexer_5_out0), .out1(demultiplexer_5_out1), .in(IDLE_q), .sel(RST));  // open: en
  I_Mapper i_mapper_1 (
    .ENABLE(stImm), .ADDi(addi), .ANDi(andi), .ORi(ori), .XORi(xori), .SLTi(slti), .SLTiU(sltiu),
    .WRITE_PC(WritePC_Imm), .WRITE_RIGESTER_FILE(WRITE_RF_Imm), .ALU_A(ALUA_SEL_Imm), .ALU_B(ALUB_SEL_Imm),
    .ALU_SELECT(ALU_SEL_Imm), .REGISTER_fILE_INPUTL(RF_Input_Imm), .REGISTER_FILE_SEL(RF_SEL_Imm),
    .BRANCH_CONTROL_SEL(BC_SEL_Imm));
  D_Flip_Flop _1_Cycle_2 (.clk(CLK), .D(WritePC_Store), .Q(StoreEnd), .reset(RST));  // open: Qn, preset, en
  D_Flip_Flop WAIT_2 (.clk(CLK), .D(demultiplexer_3_out1), .Q(CS_EN_pop), .reset(RST));  // open: Qn, preset, en
  Demultiplexer demultiplexer_6 (
    .out0(demultiplexer_6_out0), .out1(demultiplexer_6_out1), .in(or_3_out), .sel(not_3_out));  // open: en
  or or_3 (or_3_out, _1_Cycle_q, CS_EN_push);
  not not_3 (not_3_out, END_CS_IN);
  R_MAPPER r_mapper_1 (
    .ADD(add), .SUB(sub), .MUL(mul), .MULU(mulu), .DIV(div), .DIVU(divu), .AND(\and ), .OR(\or ),
    .NOR(\nor ), .XOR(\xor ), .MFHI(mfhi), .MFLO(mflo), .JR(jr), .SLT(slt), .SLTU(sltu), .NOP(nop),
    .ENABLE(stZero), .RF_SEL(RF_SEL_Zero), .ALU_SEL(ALU_SEL_Zero), .BC_SEL(BC_SEL_Zero),
    .WRITE_PC(WritePC_Zero), .UNSIGNED(\unsigned ), .WRITE_RF(WRITE_RF_Zero), .RF_INPUT(RF_Input_Zero));
  or or_4 (or_4_out, demultiplexer_4_out0, BC_SEL_Branch[0]);
  D_Flip_Flop WAIT_3 (.clk(CLK), .D(demultiplexer_6_out1), .Q(CS_EN_push), .reset(RST));  // open: Qn, preset, en
  or or_5 (CS_EN_Instruction, next, demultiplexer_5_out0);
  D_Flip_Flop _1_CYCLE_3 (.clk(CLK), .D(or_4_out), .Q(BranchEnd), .reset(RST));  // open: Qn, preset, en
  D_Flip_Flop _1_Cycle_4 (.clk(CLK), .D(RF_Input_pop[0]), .Q(ALUA_pop), .reset(RST));  // open: Qn, preset, en
  or or_6 (or_6_out, CS_EN_Instruction, WAIT_READ_q);
  Demultiplexer demultiplexer_7 (
    .out0(out_7), .out1(demultiplexer_7_out1), .in(or_6_out), .sel(not_4_out));  // open: en
  not not_4 (not_4_out, END_CS_IN);
  Demultiplexer demultiplexer_8 (
    .out0(demultiplexer_8_out0), .out1(demultiplexer_8_out1), .in(stSpecial), .sel(halt_t));  // open: en
  or or_7 (WritePC_stack, ALUA_pop, demultiplexer_6_out0);
  Demultiplexer demultiplexer_9 (
    .out0(RF_SEL_rnd_kbd[1]), .out1(TTY_ENABLE), .in(demultiplexer_8_out0), .sel(push_tty));  // open: en
  or or_8 (or_8_out, demultiplexer_8_out1, halt);
  D_Flip_Flop _1_Cycle_5 (.clk(CLK), .D(WritePC_stack), .Q(StackEnd), .reset(RST));  // open: Qn, preset, en
  D_Flip_Flop WAIT_READ (.clk(CLK), .D(demultiplexer_7_out1), .Q(WAIT_READ_q), .reset(RST));  // open: Qn, preset, en
  D_Flip_Flop _1_CYCLE_6 (.clk(CLK), .D(stZero), .Q(ZeroEnd), .reset(RST));  // open: Qn, preset, en
  D_Flip_Flop _1_CYCLE_7 (.clk(CLK), .D(stImm), .Q(ImmEnd), .reset(RST));  // open: Qn, preset, en
  Demultiplexer demultiplexer_10 (
    .out0(DIn_SEL), .out1(RF_Input_rnd[2]), .in(RF_SEL_rnd_kbd[1]), .sel(rnd));  // open: en
  D_Flip_Flop u_Halt (.clk(CLK), .D(or_8_out), .Q(halt), .reset(RST));  // open: Qn, preset, en
  D_Flip_Flop WAIT_READ_2 (.clk(CLK), .D(out_7), .Q(WAIT_READ_2_q), .reset(RST));  // open: Qn, preset, en
  or or_9 (or_9_out, stLoad_Word, ALUB_SEL_Load[0]);
  Demultiplexer demultiplexer_11 (
    .out0(RF_SEL_Load[0]), .out1(demultiplexer_11_out1), .in(or_9_out), .sel(not_5_out));  // open: en
  not not_5 (not_5_out, END_CS_IN);
  or or_10 (ALUA_stack, ALUA_pop, ALU_SEL_push[0]);
  and and_1 (stZero, WAIT_READ_2_q, zero);
  and and_2 (stImm, WAIT_READ_2_q, immediate);
  and and_3 (stBranch, WAIT_READ_2_q, branch);
  and and_4 (stLoad_Word, WAIT_READ_2_q, load_Word);
  and and_5 (stStore_Word, WAIT_READ_2_q, store_Word);
  D_Flip_Flop WAIT_4 (.clk(CLK), .D(demultiplexer_11_out1), .Q(ALUB_SEL_Load[0]), .reset(RST));  // open: Qn, preset, en
  assign ALUB_stack = {2{ALUA_pop}} | {2{ALU_SEL_push[0]}};  // OR_Gate or_11, 2 bits wide
  or or_12 (WRTE_RF_stack, RF_Input_pop[0], ALUA_pop, ALU_SEL_push[0]);
  or or_13 (CS_EN_stack, CS_EN_push, CS_EN_pop);
  assign MA_SEL_stack = {CS_EN_pop, 1'b0} | {CS_EN_push, 1'b0};  // OR_Gate or_14, 2 bits wide
  or or_15 (immediate, addi, andi, ori, xori, slti, sltiu);
  or or_16 (branch, beq, bne, blez, bgtz, bltz);
  D_Flip_Flop _1_CYCLE_8 (.clk(CLK), .D(BC_SEL_Jmp[1]), .Q(jmpEnd), .reset(RST));  // open: Qn, preset, en
  D_Flip_Flop _1_Cycle_9 (.clk(CLK), .D(RF_SEL_Load[0]), .Q(LoadEnd), .reset(RST));  // open: Qn, preset, en
  or or_17 (or_17_out, DIn_SEL, RF_Input_rnd[2], TTY_ENABLE);
  and and_6 (stSpecial, WAIT_READ_2_q, special);
  and and_7 (stStack, WAIT_READ_2_q, stack);
  and and_8 (BC_SEL_Jmp[1], WAIT_READ_2_q, jmp);
  or or_18 (next, jmpEnd, ZeroEnd, ImmEnd, BranchEnd, LoadEnd, StoreEnd, SpecialEnd, StackEnd);
  D_Flip_Flop _1_Cycle_10 (.clk(CLK), .D(or_17_out), .Q(SpecialEnd), .reset(RST));  // open: Qn, preset, en
  assign ALU_SEL = ALU_SEL_Zero | ALU_SEL_Imm | {3'b000, ALU_SEL_push[0]};  // OR_Gate or_19, 4 bits wide
  or or_20 (CS, CS_EN_Instruction, ALUB_SEL_Load[0], DOut_SEL, CS_EN_stack);
  assign ALUB = ALUB_SEL_Imm | ALUB_stack | {1'b0, DOut_SEL} | {1'b0, ALUB_SEL_Load[0]};  // OR_Gate or_21, 2 bits wide
  or or_22 (ALUA, ALUA_SEL_Imm, ALUA_stack);
  assign RFInput = RF_Input_Zero | RF_Input_Imm | {2'b00, RF_SEL_Load[0]} | {2'b00, DIn_SEL} | {RF_Input_rnd[2], 2'b00} | {2'b00, RF_Input_pop[0]};  // OR_Gate or_23, 3 bits wide
  assign RF_SEL = RF_SEL_Zero | RF_SEL_Imm | {RF_Input_pop[0], 1'b0} | {1'b0, RF_SEL_Load[0]} | {RF_SEL_rnd_kbd[1], 1'b0};  // OR_Gate or_24, 2 bits wide
  assign BCSelector = BC_SEL_Zero | BC_SEL_Imm | {1'b0, BC_SEL_Branch[0]} | {2{BC_SEL_Jmp[1]}};  // OR_Gate or_25, 2 bits wide
  or or_26 (writeRF, WRITE_RF_Zero, WRITE_RF_Imm, RF_SEL_Load[0], RF_SEL_rnd_kbd[1], WRTE_RF_stack);
  or or_27 (writePC, WritePC_Zero, WritePC_Imm, stBranch, RF_SEL_Load[0], BC_SEL_Jmp[1], WritePC_Store, RF_SEL_rnd_kbd[1], TTY_ENABLE, WritePC_stack);
  assign MA_SEL = {1'b0, DOut_SEL} | {1'b0, ALUB_SEL_Load[0]} | MA_SEL_stack;  // OR_Gate or_28, 2 bits wide
  or or_29 (RAM_RW, DOut_SEL, CS_EN_push);

  assign KBD_EN = DIn_SEL;

  // Other names for the same wires on the sheet: ALU_SEL_stack[0] = ALU_SEL_push[0]; ALUA_push = ALU_SEL_push[0];
  //   ALUB_push[1:0] = {2{ALU_SEL_push[0]}}; WRITE_RF_push0 = ALU_SEL_push[0]; ALUB_pop[1:0] = {2{ALUA_pop}};
  //   WRITE_RF_pop1 = ALUA_pop; BC_SEL_Jmp[0] = BC_SEL_Jmp[1]; stJmp = BC_SEL_Jmp[1]; WritePC_Jmp = BC_SEL_Jmp[1];
  //   Flag_SEL[2:0] = FlagSelector; haltOut = halt; CS_EN_Load = ALUB_SEL_Load[0]; MA_SEL_Load[0] = ALUB_SEL_Load[0];
  //   MA_SEL_pop[1] = CS_EN_pop; MA_SEL_push[1] = CS_EN_push; RAM_RW_push = CS_EN_push; RAM_RW_stack = CS_EN_push;
  //   ALUB_SEL_Store[0] = DOut_SEL; CS_EN_Store = DOut_SEL; DOut_SEL_Store = DOut_SEL; MA_SEL_Store[0] = DOut_SEL;
  //   RAM_RW_store = DOut_SEL; DIn_SEL_kbd = DIn_SEL; RF_Input_kbd[0] = DIn_SEL; WRITE_RF_rnd_kbd = RF_SEL_rnd_kbd[1];
  //   WritePC_rnd_kbd = RF_SEL_rnd_kbd[1]; RF_Input_stack[0] = RF_Input_pop[0]; RF_SEL_pop[1] = RF_Input_pop[0];
  //   RF_SEL_stack[1] = RF_Input_pop[0]; WRITE_RF_pop0 = RF_Input_pop[0]; RFInput_Load[0] = RF_SEL_Load[0];
  //   WRITE_RF_Load = RF_SEL_Load[0]; WritePC_Load = RF_SEL_Load[0]; WritePC_Branch = stBranch; Write_ID = out_7;
  //   TTY_EN = TTY_ENABLE; WritePC_TTY = TTY_ENABLE

  // Notes on the sheet:
  //   kbd
endmodule

module Func_Code_Decoder (
  input  f1,
  input  f2,
  input  f3,
  input  f4,
  input  f5,
  input  f6,
  input  enable,
  output AND,
  output ADD,
  output DIV,
  output NOP_POP,
  output RND,
  output OR,
  output SUB,
  output DIVU,
  output PUSH_TTY,
  output KBD,
  output XOR,
  output MUL,
  output SLT,
  output HALT,
  output NOR,
  output MULU,
  output SLTU,
  output MFHI,
  output MFLO,
  output JR
);

  wire and_1_out, and_2_out, and_3_out, and_4_out, and_5_out, and_6_out, and_7_out, and_15_out, and_16_out,
       and_17_out, and_18_out, and_23_out, and_24_out, and_25_out, and_26_out, and_31_out, and_32_out,
       and_33_out, and_37_out, and_38_out;

  and and_1 (and_1_out, ~f1, ~f2, f3, ~f4, ~f5, f6);  // AND_Gate
  and and_2 (and_2_out, f1, ~f2, f3, ~f4, ~f5, f6);  // AND_Gate
  and and_3 (and_3_out, ~f1, ~f2, ~f3, f4, ~f5, f6);  // AND_Gate
  and and_4 (and_4_out, f1, f2, f3, ~f4, ~f5, f6);  // AND_Gate
  and and_5 (and_5_out, ~f1, ~f2, ~f3, ~f4, f5, ~f6);  // AND_Gate
  and and_6 (and_6_out, ~f1, f2, ~f3, ~f4, f5, ~f6);  // AND_Gate
  and and_7 (and_7_out, ~f1, ~f2, ~f3, f4, ~f5, ~f6);  // AND_Gate
  and and_8 (AND, and_1_out, enable);
  and and_9 (OR, and_2_out, enable);
  and and_10 (XOR, and_3_out, enable);
  and and_11 (NOR, and_4_out, enable);
  and and_12 (MFHI, and_5_out, enable);
  and and_13 (MFLO, and_6_out, enable);
  and and_14 (JR, and_7_out, enable);
  and and_15 (and_15_out, ~f1, ~f2, ~f3, ~f4, ~f5, f6);  // AND_Gate
  and and_16 (and_16_out, ~f1, f2, ~f3, ~f4, ~f5, f6);  // AND_Gate
  and and_17 (and_17_out, ~f1, ~f2, ~f3, f4, f5, ~f6);  // AND_Gate
  and and_18 (and_18_out, f1, ~f2, ~f3, f4, f5, ~f6);  // AND_Gate
  and and_19 (ADD, and_15_out, enable);
  and and_20 (SUB, and_16_out, enable);
  and and_21 (MUL, and_17_out, enable);
  and and_22 (MULU, and_18_out, enable);
  and and_23 (and_23_out, ~f1, f2, ~f3, f4, f5, ~f6);  // AND_Gate
  and and_24 (and_24_out, f1, f2, ~f3, f4, f5, ~f6);  // AND_Gate
  and and_25 (and_25_out, ~f1, f2, ~f3, f4, ~f5, f6);  // AND_Gate
  and and_26 (and_26_out, f1, f2, ~f3, f4, ~f5, f6);  // AND_Gate
  and and_27 (DIV, and_23_out, enable);
  and and_28 (DIVU, and_24_out, enable);
  and and_29 (SLT, and_25_out, enable);
  and and_30 (SLTU, and_26_out, enable);
  and and_31 (and_31_out, ~f1, ~f2, ~f3, ~f4, ~f5, ~f6);  // AND_Gate
  and and_32 (and_32_out, f1, ~f2, ~f3, ~f4, ~f5, ~f6);  // AND_Gate
  and and_33 (and_33_out, f1, f2, f3, f4, f5, f6);
  and and_34 (NOP_POP, and_31_out, enable);
  and and_35 (PUSH_TTY, and_32_out, enable);
  and and_36 (HALT, and_33_out, enable);
  and and_37 (and_37_out, ~f1, f2, ~f3, ~f4, ~f5, ~f6);  // AND_Gate
  and and_38 (and_38_out, ~f1, ~f2, f3, ~f4, ~f5, ~f6);  // AND_Gate
  and and_39 (RND, and_37_out, enable);
  and and_40 (KBD, and_38_out, enable);

  // Other names for the same wires on the sheet: En = enable
endmodule

module Op_Code_Decoder (
  input  o1,
  input  o2,
  input  o3,
  input  o4,
  input  o5,
  input  o6,
  input  enable,
  output ZERO,
  output XORi,
  output STACK,
  output ADDi,
  output SLTi,
  output SPECIAL,
  output ANDi,
  output SLTiU,
  output JUMP,
  output ORi,
  output BEQ,
  output BLTZ,
  output BNE,
  output LW,
  output BLEZ,
  output SW,
  output BGTZ
);

  wire and_1_out, and_2_out, and_3_out, and_4_out, and_9_out, and_10_out, and_11_out, and_12_out, and_17_out,
       and_18_out, and_19_out, and_23_out, and_24_out, and_25_out, and_29_out, and_30_out, and_31_out;

  and and_1 (and_1_out, ~o1, ~o2, o3, ~o4, ~o5, ~o6);  // AND_Gate
  and and_2 (and_2_out, o1, ~o2, o3, ~o4, ~o5, ~o6);  // AND_Gate
  and and_3 (and_3_out, ~o1, o2, o3, ~o4, ~o5, ~o6);  // AND_Gate
  and and_4 (and_4_out, o1, o2, o3, ~o4, ~o5, ~o6);  // AND_Gate
  and and_5 (BEQ, and_1_out, enable);
  and and_6 (BNE, and_2_out, enable);
  and and_7 (BLEZ, and_3_out, enable);
  and and_8 (BGTZ, and_4_out, enable);
  and and_9 (and_9_out, ~o1, ~o2, ~o3, ~o4, ~o5, ~o6);  // AND_Gate
  and and_10 (and_10_out, ~o1, ~o2, ~o3, o4, ~o5, ~o6);  // AND_Gate
  and and_11 (and_11_out, ~o1, ~o2, o3, o4, ~o5, ~o6);  // AND_Gate
  and and_12 (and_12_out, o1, ~o2, o3, o4, ~o5, ~o6);  // AND_Gate
  and and_13 (ZERO, and_9_out, enable);
  and and_14 (ADDi, and_10_out, enable);
  and and_15 (ANDi, and_11_out, enable);
  and and_16 (ORi, and_12_out, enable);
  and and_17 (and_17_out, o1, ~o2, ~o3, ~o4, ~o5, ~o6);  // AND_Gate
  and and_18 (and_18_out, o1, o2, ~o3, ~o4, ~o5, o6);  // AND_Gate
  and and_19 (and_19_out, o1, o2, ~o3, o4, ~o5, o6);  // AND_Gate
  and and_20 (BLTZ, and_17_out, enable);
  and and_21 (LW, and_18_out, enable);
  and and_22 (SW, and_19_out, enable);
  and and_23 (and_23_out, ~o1, o2, o3, o4, ~o5, ~o6);  // AND_Gate
  and and_24 (and_24_out, ~o1, o2, ~o3, o4, ~o5, ~o6);  // AND_Gate
  and and_25 (and_25_out, o1, o2, ~o3, o4, ~o5, ~o6);  // AND_Gate
  and and_26 (XORi, and_23_out, enable);
  and and_27 (SLTi, and_24_out, enable);
  and and_28 (SLTiU, and_25_out, enable);
  and and_29 (and_29_out, ~o1, ~o2, ~o3, o4, o5, o6);  // AND_Gate
  and and_30 (and_30_out, o1, o2, o3, o4, o5, o6);
  and and_31 (and_31_out, ~o1, o2, ~o3, ~o4, ~o5, ~o6);  // AND_Gate
  and and_32 (STACK, and_29_out, enable);
  and and_33 (SPECIAL, and_30_out, enable);
  and and_34 (JUMP, and_31_out, enable);

  // Other names for the same wires on the sheet: _06 = o6; En = enable
endmodule

module I_Mapper (
  input  ENABLE,
  input  ADDi,
  input  ANDi,
  input  ORi,
  input  XORi,
  input  SLTi,
  input  SLTiU,
  output WRITE_PC,
  output WRITE_RIGESTER_FILE,
  output ALU_A,
  output [1:0] ALU_B,
  output [3:0] ALU_SELECT,
  output [2:0] REGISTER_fILE_INPUTL,
  output [1:0] REGISTER_FILE_SEL,
  output [1:0] BRANCH_CONTROL_SEL
);

  wire ALU_SEL0, ALU_SEL2, ALU_SEL3;
  wire [1:0] or_1_out;

  and and_1 (WRITE_PC, ENABLE, 1'b1);
  and and_2 (WRITE_RIGESTER_FILE, ENABLE, 1'b1);
  or or_1 (or_1_out[0], ADDi, SLTi, SLTiU);
  or or_2 (or_1_out[1], ANDi, ORi, XORi);
  assign ALU_B = {2{ENABLE}} & or_1_out;  // AND_Gate and_3, 2 bits wide
  or or_3 (ALU_SEL3, SLTi, SLTiU);
  or or_4 (ALU_SEL0, ORi, XORi, SLTiU);
  or or_5 (ALU_SEL2, ANDi, ORi, XORi);
  assign ALU_SELECT = {4{ENABLE}} & {ALU_SEL3, ALU_SEL2, XORi, ALU_SEL0};  // AND_Gate and_4, 4 bits wide

  assign ALU_A = 1'b0;
  assign BRANCH_CONTROL_SEL = 2'b00;
  assign REGISTER_fILE_INPUTL = 3'b000;
  assign REGISTER_FILE_SEL = {1'b0, ENABLE};

  // Other names for the same wires on the sheet: ALU_SEL1 = XORi; EN = ENABLE
endmodule

module R_MAPPER (
  input  ADD,
  input  SUB,
  input  MUL,
  input  MULU,
  input  DIV,
  input  DIVU,
  input  AND,
  input  OR,
  input  NOR,
  input  XOR,
  input  MFHI,
  input  MFLO,
  input  JR,
  input  SLT,
  input  SLTU,
  input  NOP,
  input  ENABLE,
  output [1:0] RF_SEL,
  output [3:0] ALU_SEL,
  output [1:0] BC_SEL,
  output WRITE_PC,
  output UNSIGNED,
  output WRITE_RF,
  output [2:0] RF_INPUT
);

  wire ALU_SEL0, ALU_SEL1, ALU_SEL2, ALU_SEL3, and_2_out, or_1_out, or_7_out;
  wire [2:2] or_6_out;

  or or_1 (or_1_out, DIV, DIVU);
  or or_2 (ALU_SEL0, SUB, SLTU, or_1_out, XOR, OR);
  or or_3 (ALU_SEL1, MULU, MUL, XOR, NOR, XOR);
  or or_4 (ALU_SEL2, NOR, XOR, OR, AND);
  or or_5 (ALU_SEL3, SLT, SLTU);
  and and_1 (WRITE_PC, ENABLE, 1'b1);
  and and_2 (and_2_out, ENABLE, ~NOP);  // AND_Gate
  and and_3 (WRITE_RF, ~JR, ~MUL, ~MULU, ~DIV, ~DIVU, and_2_out);  // AND_Gate
  or or_6 (or_6_out[2], MFHI, MFLO);
  assign ALU_SEL = {4{ENABLE}} & {ALU_SEL3, ALU_SEL2, ALU_SEL1, ALU_SEL0};  // AND_Gate and_4, 4 bits wide
  assign RF_INPUT = {3{ENABLE}} & {or_6_out[2], MFLO, MFHI};  // AND_Gate and_5, 3 bits wide
  and and_6 (BC_SEL[1], JR, ENABLE);
  or or_7 (or_7_out, MULU, DIVU);
  assign RF_SEL = 2'b10 & {2{ENABLE}};  // AND_Gate and_7, 2 bits wide
  and and_8 (UNSIGNED, ENABLE, or_7_out);

  assign BC_SEL[0] = 1'b0;

  // Other names for the same wires on the sheet: EN = ENABLE
endmodule

module Branch_Mapper (
  input  BEQ,
  input  BNE,
  input  BLEZ,
  input  BGTZ,
  input  BLTZ,
  output [2:0] Flag_Sel
);

  or or_1 (Flag_Sel[0], BLEZ, BLTZ);
  or or_2 (Flag_Sel[1], BGTZ, BLTZ);

  assign Flag_Sel[2] = BNE;
endmodule

module Data_Path_2 (
  input  CLK,
  input  Reset,
  input  [1:0] RegDest,
  input  [2:0] MemtoReg,
  input  ALUSrcA,
  input  [1:0] ALUSrcB,
  input  [3:0] ALUControl,
  input  [2:0] in_8,
  input  in_9,
  input  in_10,
  input  [1:0] in_11,
  input  [1:0] in_12,
  input  in_13,
  input  in_14,
  input  in_15,
  input  [31:0] DataIn,
  output Flag,
  output [31:0] Data_Out,
  output [3:0] Mask,
  output [1:0] Offset,
  output [15:0] Address,
  output [6:0] TTY_DATA,
  output [5:0] op_code,
  output [5:0] func
);

  wire equ, gtz, hi_lo, letz, ltz, n_equ;
  wire [4:0] multiplexer_1_out, Rd, Rs, Rt;
  wire [15:0] \const ;
  wire [25:0] address_t;
  wire [31:0] _0_const, ALUOut, branch_control_1_pc_2, Hi, Lo, multiplexer_2_out, multiplexer_3_out,
       multiplexer_4_out, multiplexer_6_out, OutHi, OutLo, PC, random, RD2, SignImm, SP;
  wire [31:7] RD1;

  // Probe on {RD1, TTY_DATA}
  // Probe on RegDest
  InstructionDecoder instructiondecoder_1 (
    .IRWrite(in_14), .CLK(CLK), .op_code(op_code), .address(address_t), .in_3(DataIn), .Rs(Rs), .Rt(Rt),
    .\const (\const ), .func(func), .Rd(Rd));
  _32x32_RF u_32x32_rf_1 (
    .Reset(Reset), .ReadData1({RD1, TTY_DATA}), .ReadData2(RD2), .WriteData(multiplexer_2_out),
    .WriteReg(multiplexer_1_out), .ReadReg1(Rs), .ReadReg2(Rt), .RegWriteEnable(in_13), .CLK(CLK),
    .OutHi(OutHi), .mult_div(hi_lo), .Hi(Hi), .Lo(Lo), .OutLo(OutLo), .SP(SP));
  // Probe on Rs
  // Probe on Rt
  // Probe on multiplexer_1_out
  Multiplexer #(.select(2), .width(5), .enable("false")) multiplexer_1 (
    .in0({5{1'b1}}), .in1(Rt), .in2(Rd), .out(multiplexer_1_out), .sel(RegDest));  // open: in3
  Multiplexer #(.select(3), .width(32), .enable("false")) multiplexer_2 (
    .in0(ALUOut), .in1(DataIn), .in4(random), .in5(OutHi), .in6(OutLo), .out(multiplexer_2_out),
    .sel(MemtoReg));  // open: in2, in3, in7
  // Probe on MemtoReg
  // Probe on multiplexer_2_out
  Multiplexer #(.width(32), .enable("false")) multiplexer_3 (
    .in0({RD1, TTY_DATA}), .in1(SP), .out(multiplexer_3_out), .sel(ALUSrcA));
  Multiplexer #(.select(2), .width(32), .enable("false")) multiplexer_4 (
    .in0(RD2), .in1(SignImm), .in2(_0_const), .in3(32'h4), .out(multiplexer_4_out), .sel(ALUSrcB));
  // Probe on ALUSrcB
  ALU_2 alu_1 (
    .in_1(multiplexer_3_out), .in_2(in_15), .in_3(ALUControl), .in_4(multiplexer_4_out), .out_6(Hi),
    .out_8(ALUOut), .out_10(Lo), .out_5(n_equ), .out_7(equ), .Mul_Div(hi_lo), .out_11(letz), .out_12(gtz),
    .out_13(ltz));
  Branch_Control branch_control_1 (
    .PC(PC), .PCSrc(in_12), .offset(\const ), .address(address_t), .RD1({RD1, TTY_DATA}),
    .PC_2(branch_control_1_pc_2));
  // Probe on ALUOut
  // Probe on PC
  Register #(.width(32)) register_1 (.D(branch_control_1_pc_2), .en(in_10), .Q(PC), .clk(CLK), .clr(Reset));
  Multiplexer #(.width(32), .enable("false")) multiplexer_5 (
    .in0({RD1, TTY_DATA}), .in1(RD2), .out(Data_Out), .sel(in_9));
  Multiplexer #(.select(2), .width(32), .enable("false")) multiplexer_6 (
    .in0(PC), .in1(ALUOut), .in2(SP),
    .out({multiplexer_6_out[31:20], Address, Offset, multiplexer_6_out[1:0]}), .sel(in_11));  // open: in3
  // Probe on _0_const
  assign _0_const = {{16{1'b0}}, \const };  // Bit_Extender bit_extender_1
  // Probe on SignImm
  assign SignImm = {{16{\const [15]}}, \const };  // Bit_Extender bit_extender_2
  Random #(.width(32)) random_1 (.clk(CLK), .out(random));  // open: next, clr
  Multiplexer #(.select(3), .enable("false")) multiplexer_7 (
    .in0(equ), .in1(letz), .in2(gtz), .in3(ltz), .in4(n_equ), .out(Flag), .sel(in_8));  // open: in5, in6, in7
  // Probe on in_8
  Decoder #(.select(2), .enable("false")) decoder_1 (
    .out0(Mask[0]), .out1(Mask[1]), .out2(Mask[2]), .out3(Mask[3]), .sel(Offset));

  // Other names for the same wires on the sheet: DOS = in_9; flagSrc[2:0] = in_8; IRWrite = in_14; MAS[1:0] = in_11;
  //   PCEn = in_10; PCSrc[1:0] = in_12; R_W = in_13; RD1[6:0] = TTY_DATA; unsigned = in_15
endmodule

module Branch_Control (
  input  [31:0] PC,
  input  [1:0] PCSrc,
  input  [15:0] offset,
  input  [25:0] address,
  input  [31:0] RD1,
  output [31:0] PC_2
);

  wire [31:0] _4_offset32, offset32, PC__4, PC__4_4_offset32;

  Adder #(.width(32)) adder_1 (.a(PC), .b(32'h4), .out(PC__4));  // open: cin, cout
  assign offset32 = {{16{offset[15]}}, offset};  // Bit_Extender bit_extender_1
  Shifter #(.width(32)) shifter_1 (.in(offset32), .\dist (5'b00010), .out(_4_offset32));
  Multiplexer #(.select(2), .width(32), .enable("false")) multiplexer_1 (
    .in0(PC__4), .in1(PC__4_4_offset32), .in2(RD1), .in3({PC[31:28], address, 2'b00}), .out(PC_2), .sel(PCSrc));
  Adder #(.width(32)) adder_2 (.a(PC__4), .b(_4_offset32), .out(PC__4_4_offset32));  // open: cin, cout

  // Other names for the same wires on the sheet: address_J[31:2] = {PC[31:28], address}
endmodule

module InstructionDecoder (
  input  IRWrite,
  input  CLK,
  input  [31:0] in_3,
  output [5:0] op_code,
  output [25:0] address,
  output [4:0] Rs,
  output [4:0] Rt,
  output [15:0] \const ,
  output [5:0] func,
  output [4:0] Rd
);

  Register #(.width(32)) register_1 (.D(in_3), .en(IRWrite), .Q({op_code, address}), .clk(CLK));  // open: clr

  assign \const  = address[15:0];
  assign func = address[5:0];
  assign Rd = address[15:11];
  assign Rs = address[25:21];
  assign Rt = address[20:16];
endmodule
